# Fritzing sketch LDR Sensor (saved by Fritzing 0.9.10b)
breadboards: 1

parts:
  U1 = ESP8266 WiFi Module [part_number=ESP8266]  # not connected
  LED1 = LED - 5mm [color="Red (633nm)" current=0.030 package="5 mm [THT]"]
  R1 = Resistor [tolerance=±5% resistance=220 package="0603 [SMD]"]
  R2 = Resistor [tolerance=±5% resistance=220 package="0603 [SMD]"]
  LED2 = LED - 5mm [color="Red (633nm)" current=0.030 package="5 mm [THT]"]

nets:
  N1: LED1.cathode, R2.Pin_1
  N2: LED1.anode, R1.Pin_1
  N3: R1.Pin_0, LED2.anode
  N4: R2.Pin_0, LED2.cathode
