# Fritzing sketch Lamp Sensor (saved by Fritzing 0.9.10b)
breadboards: 2

parts:
  R1 = Resistor [tolerance=±5% power=0.25 resistance=220 package=THT]
  LED2 = smd LED [color="Red (633nm)" package="0603 [SMD]"]
  R2 = Resistor [tolerance=±5% power=0.25 resistance=220 package=THT]
  LED3 = smd LED [color="Red (633nm)" package="0603 [SMD]"]
  R3 = Resistor [tolerance=±5% power=0.25 resistance=220 package=THT]
  LED4 = smd LED [color="Red (633nm)" package="0603 [SMD]"]
  U1 = ESP8266 WiFi Module [part_number=ESP8266]
  M1 = CK-07 [package=THT]
  WeMos_D1_Mini1 = WeMos D1 Mini
  R4 = Resistor [tolerance=±5% power=0.25 resistance=220 package=THT]
  R5 = Resistor [tolerance=±5% power=0.25 resistance=220 package=THT]
  R6 = Resistor [tolerance=±5% power=0.25 resistance=220 package=THT]
  LED5 = smd LED [color="Red (633nm)" package="0603 [SMD]"]
  LED6 = smd LED [color="Red (633nm)" package="0603 [SMD]"]
  LED7 = smd LED [color="Red (633nm)" package="0603 [SMD]"]
  M2 = CK-07 [package=THT]

nets:
  N1: R1.Pin_0, LED2.anode
  N2: R1.Pin_1, R2.Pin_1, R3.Pin_1, U1.GND
  N3: LED2.cathode, LED3.cathode, LED4.cathode, U1.VCC, M1.pin_4
  N4: R2.Pin_0, LED3.anode
  N5: R3.Pin_0, LED4.anode
  N6: WeMos_D1_Mini1.5V, M2.pin_4
  N7: WeMos_D1_Mini1.A0, M2.pin_1
  N8: WeMos_D1_Mini1.D0, M2.pin_2
  N9: WeMos_D1_Mini1.D6, R4.Pin_0, LED5.anode
  N10: WeMos_D1_Mini1.D7, LED7.cathode
  N11: WeMos_D1_Mini1.D8, LED6.cathode
  N12: WeMos_D1_Mini1.G, R4.Pin_1, R5.Pin_1, R6.Pin_1, M2.pin_3
  N13: R5.Pin_0, LED6.anode
  N14: R6.Pin_0, LED7.anode

custom parts:
  CK-07: Fc-51 Infrared Obstacle Avoidance Proximity Sensor module. IR transmitter led, receiver LED, lm393 compaitor and a pot. 3.3 V to 5V power.
  WeMos D1 Mini: The D1 mini is a mini wifi board based on ESP-8266EX.
