# Fritzing sketch Lamp Sensor2 (saved by Fritzing 0.9.10b)
breadboards: 1

parts:
  WeMos_D1_Mini1 = WeMos D1 Mini
  R4 = Resistor [tolerance=±5% power=0.25 resistance=220 package=THT]
  R5 = Resistor [tolerance=±5% power=0.25 resistance=220 package=THT]
  R6 = Resistor [tolerance=±5% power=0.25 resistance=220 package=THT]
  LED5 = smd LED [color="Red (633nm)" package="0603 [SMD]"]
  LED6 = smd LED [color="Red (633nm)" package="0603 [SMD]"]
  LED7 = smd LED [color="Red (633nm)" package="0603 [SMD]"]
  M2 = CK-07 [package=THT]

nets:
  N1: WeMos_D1_Mini1.5V, M2.pin_4
  N2: WeMos_D1_Mini1.A0, M2.pin_1
  N3: WeMos_D1_Mini1.D0, M2.pin_2
  N4: WeMos_D1_Mini1.D6, R4.Pin_0, LED5.anode
  N5: WeMos_D1_Mini1.D7, LED7.cathode
  N6: WeMos_D1_Mini1.D8, LED6.cathode
  N7: WeMos_D1_Mini1.G, R4.Pin_1, R5.Pin_1, R6.Pin_1, M2.pin_3
  N8: R5.Pin_0, LED6.anode
  N9: R6.Pin_0, LED7.anode

custom parts:
  WeMos D1 Mini: The D1 mini is a mini wifi board based on ESP-8266EX.
  CK-07: Fc-51 Infrared Obstacle Avoidance Proximity Sensor module. IR transmitter led, receiver LED, lm393 compaitor and a pot. 3.3 V to 5V power.
